# Fritzing sketch espresso_switch (saved by Fritzing 0.9.3b)
breadboards: 1

parts:
  WeMos_D1_Mini1 = WeMos D1 Mini
  U1 = TLP621 [package=THT]
  R1 = Resistor [tolerance=±5% resistance=100 package="1206 [SMD]"]
  R2 = Resistor [tolerance=±5% resistance=100 package="0805 [SMD]"]
  S1 = Pushbutton [package="[THT]"]
  S2 = Pushbutton [package="[THT]"]
  R3 = Resistor [tolerance=±5% resistance=33k package="1206 [SMD]"]
  U2 = RELAY-SOLIDSTATE [package=relay-s108t02]

nets:
  N1: WeMos_D1_Mini1.3V3, R1.Pin_0
  N2: WeMos_D1_Mini1.D2, S2.Pin_3, S2.Pin_4
  N3: WeMos_D1_Mini1.D4, U2.+
  N4: WeMos_D1_Mini1.D6, U1.Pin_3
  N5: WeMos_D1_Mini1.G, S1.Pin_1, S1.Pin_2, S2.Pin_1, S2.Pin_2, R3.Pin_0, U2.-
  N6: U1.Pin_1, R2.Pin_1
  N7: U1.Pin_2, S1.Pin_3, S1.Pin_4
  N8: U1.Pin_4, R1.Pin_1

notes:
  Button 1 - simulates espresso power sense (default = off)
  Button 2 - reset settings button, hold 10s to activate and reset wifi + homekit
  relay - output for the espresso momentary switch circuit
