# Fritzing sketch espresso_switch (saved by Fritzing 0.9.3b)
circuit board: 8.46667cm x 5.64444cm
breadboards: 1

parts:
  WeMos_D1_Mini1 = WeMos D1 Mini
  U1 = TLP621 [package=THT]
  R2 = Resistor [tolerance=±5% resistance=100 package="0805 [SMD]"]
  U2 = RELAY-SOLIDSTATE [package=relay-s108t02]
  R4 = Resistor [tolerance=±5% resistance=100 package="0805 [SMD]"]
  R5 = Resistor [tolerance=±5% resistance=100 package="0805 [SMD]"]
  S1 = Pushbutton [package="[SMD]"]
  JP2 = Header 2 [package=molex-1x2_lock]
  HLK-PM1 = HLK-PM01
  JP3 = Header 2 [package=molex-1x2_lock]
  LED1 = LED - 3mm [color="Red (633nm)" package="3 mm [THT]"]
  JP1 = Header 2 [package=molex-1x2_lock]
  Q1 = TRANSISTOR_NPN [package=to-92]
  R6 = Resistor [tolerance=±5% resistance=1k package="1206 [SMD]"]
  R7 = Resistor [tolerance=±5% resistance=10k package="1206 [SMD]"]
  D1 = Rectifier Diode [part_number=1N4001 package="300 mil [THT]"]

nets:
  N1: WeMos_D1_Mini1.5V, R2.Pin_0, HLK-PM1.+Vo, Q1.E
  N2: WeMos_D1_Mini1.D2, S1.Pin_3, S1.Pin_4
  N3: WeMos_D1_Mini1.D4, LED1.cathode
  N4: WeMos_D1_Mini1.D5, R6.Pin_0
  N5: WeMos_D1_Mini1.D6, U1.Pin_3
  N6: WeMos_D1_Mini1.G, U1.Pin_4, R4.Pin_1, R5.Pin_1, S1.Pin_1, S1.Pin_2, JP2.2, HLK-PM1.-Vo, R7.Pin_0, D1.anode
  N7: U1.Pin_1, R2.Pin_1
  N8: U1.Pin_2, JP2.1
  N9: U2.T1, JP1.1
  N10: U2.T2, JP1.2
  N11: U2.+, Q1.C, D1.cathode
  N12: U2.-, R4.Pin_0
  N13: R5.Pin_0, LED1.anode
  N14: HLK-PM1.AC#0, JP3.1
  N15: HLK-PM1.AC#1, JP3.2
  N16: Q1.B, R6.Pin_1, R7.Pin_1

notes:
  DC connector - espresso power sense (LOW = off)
  button - reset settings button, hold 10s to activate and reset wifi & homekit, press to toggle espresso power
  AC/DC relay - output for the espresso momentary switch circuit. 5v logic level from 3v3 converted by the NPN transistor
  LED indicates the status of the device
  banded wires are (from left to right): DC power sense (up to 30V), AC/DC Relay for power toggle and AC Mains supply voltage
